# Fritzing sketch twodigit (saved by Fritzing 0.9.10b)
circuit board: 4.49982cm x 3.03156cm
breadboards: 1

parts:
  LED1 = 2-digit 7-segment [package=THT-longpads]
  U1 = 74HC595 [package="DIP16 [THT]"]
  R1 = Resistor [tolerance=±5% resistance=330 package="2010 [SMD]"]
  R2 = Resistor [tolerance=±5% resistance=330 power=0.5W package="2512 [SMD]"]
  Mod1 = Raspberry Pi Pico

nets:
  N1: LED1.A, U1.Q0
  N2: LED1.C, U1.Q2
  N3: LED1.DP, U1.Q7
  N4: LED1.E, U1.Q4
  N5: LED1.D, U1.Q3
  N6: LED1.G, U1.Q6
  N7: LED1.F, U1.Q5
  N8: LED1.DIG2, R2.Pin_0
  N9: LED1.DIG1, R1.Pin_0
  N10: LED1.B, U1.Q1
  N11: R1.Pin_1, Mod1.pin_16
  N12: R2.Pin_1, Mod1.pin_21

custom parts:
  2-digit 7-segment: Most common two-digit seven-segment led indicator you can find on the internet. 10 legs: 2 common electrodes (one per each digit), 8 electrodes of each segment.
  Raspberry Pi Pico: Raspberry Pi Pico. Based around the RP2040 microcontroller the Pico is a low cost microcontroller device bringing Raspberry Pi quality, cost, and easy of use to the microcontroller space. Jan 2021, Split part in to two versions: tht (this one) and SMD. This one will drill holes for a .1 in header in pcb to allow plugging in the module as well as providing pads to solder the module to the top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
